// Logisim project PROJECT 6.circ as structural Verilog: 1 circuit, main circuit main
module main (
  input  D3,
  input  PR,
  input  CLR,
  output Q3,
  output Q2,
  output Q1,
  output Q
);

  wire CLK_out;

  Clock CLK (.out(CLK_out));
  D_Flip_Flop _1 (.clk(CLK_out), .D(D3), .Q(Q3), .preset(PR), .reset(CLR));  // open: Qn, en
  D_Flip_Flop _0 (.clk(CLK_out), .D(Q3), .Q(Q2), .preset(PR), .reset(CLR));  // open: Qn, en
  D_Flip_Flop _1_2 (.clk(CLK_out), .D(Q2), .Q(Q1), .preset(PR), .reset(CLR));  // open: Qn, en
  D_Flip_Flop d_ff_1 (.clk(CLK_out), .D(Q1), .Q(Q), .preset(PR), .reset(CLR));  // open: Qn, en
endmodule
