// Logisim project SERIL IN PARALLEL OUT.circ as structural Verilog: 1 circuit, main circuit main
module main (
  input  in_1,
  input  in_2,
  input  in_3,
  input  in_4,
  input  in_5,
  output out_6
);

  wire and_1_out, and_2_out, and_3_out, and_4_out, and_5_out, and_6_out, clock_1_out, d_ff_1_q, d_ff_2_q,
       d_ff_3_q, not_1_out, or_1_out, or_2_out, or_3_out, undriven, undriven_2, undriven_3, undriven_4,
       undriven_5;

  not not_1 (not_1_out, in_5);
  Clock clock_1 (.out(clock_1_out));
  and and_1 (and_1_out, d_ff_1_q, in_5);
  D_Flip_Flop d_ff_1 (.clk(undriven), .Q(d_ff_1_q), .en(clock_1_out));  // open: D, Qn, preset, reset
  and and_2 (and_2_out, not_1_out, undriven_2);
  or or_1 (or_1_out, and_1_out, and_2_out);
  D_Flip_Flop d_ff_2 (.clk(or_1_out), .Q(d_ff_2_q), .en(clock_1_out));  // open: D, Qn, preset, reset
  and and_3 (and_3_out, d_ff_2_q, in_5);
  or or_2 (or_2_out, and_3_out, and_4_out);
  and and_4 (and_4_out, not_1_out, undriven_3);
  D_Flip_Flop d_ff_3 (.clk(or_2_out), .Q(d_ff_3_q), .en(clock_1_out));  // open: D, Qn, preset, reset
  and and_5 (and_5_out, d_ff_3_q, in_5);
  or or_3 (or_3_out, and_5_out, and_6_out);
  and and_6 (and_6_out, not_1_out, undriven_5);
  D_Flip_Flop d_ff_4 (.clk(undriven_4), .D(or_3_out), .Qn(out_6), .en(clock_1_out));  // open: Q, preset, reset
endmodule
