// Logisim project SR FLIP FLOP edge triggered sr storage.circ as structural Verilog: 1 circuit, main circuit main
module main (
  input  in_1,
  input  in_2,
  output out_3,
  output out_4
);

  wire nand_1_out, undriven;

  nand nand_1 (nand_1_out, in_1, undriven);
  nand nand_2 (out_3, undriven, in_2);
  nand nand_3 (out_3, nand_1_out, out_4);
  not nand_4 (out_4, out_3);  // NAND_Gate
endmodule
