// Logisim project SR Latch first memory elementy.circ as structural Verilog: 1 circuit, main circuit main
module main (
  input  in_1,
  input  in_2,
  output out_3,
  output out_4
);

  wire nand_1_out, not_1_out;

  not not_1 (not_1_out, in_1);
  nand nand_1 (nand_1_out, in_1, in_2);
  nand nand_2 (out_3, in_2, not_1_out);
  nand nand_3 (out_3, nand_1_out, out_4);
  not nand_4 (out_4, out_3);  // NAND_Gate
endmodule
